// Logisim project e2310647.circ as structural Verilog: 1 circuit, main circuit main
module main (
  input  A1,
  input  A0,
  input  B1,
  input  B0,
  output X,
  output Y
);

  wire and_1_out, and_2_out, and_3_out, and_4_out, and_5_out, and_6_out, not_1_out, not_2_out, not_3_out,
       not_4_out, not_5_out, not_6_out, or_1_out, or_2_out;

  not not_1 (not_1_out, B1);
  not not_2 (not_2_out, B0);
  or or_1 (or_1_out, A1, not_1_out);
  and and_1 (and_1_out, A0, not_2_out);
  or or_2 (or_2_out, A0, not_2_out);
  and and_2 (and_2_out, A1, not_1_out);
  not not_3 (not_3_out, or_1_out);
  not not_4 (not_4_out, and_1_out);
  not not_5 (not_5_out, or_2_out);
  not not_6 (not_6_out, and_2_out);
  and and_3 (and_3_out, not_3_out, not_4_out);
  and and_4 (and_4_out, or_2_out, and_2_out);
  or or_3 (X, and_3_out, and_4_out);
  and and_5 (and_5_out, or_1_out, and_1_out);
  and and_6 (and_6_out, not_5_out, not_6_out);
  or or_4 (Y, and_5_out, and_6_out);
endmodule
